// Logisim project MiniComputer.circ as structural Verilog: 8 circuits, main circuit MiniComputer
module TEST_PLAYGROUND (
  input  [7:0] DATA_IN,
  input  BUS_SEL__CHIP,
  input  RST,
  input  nSEL,
  input  BUS_SEL__other,
  input  [1:0] DATA__D0_D1,
  input  TSM_END__other
);

  wire clock_1_out;
  wire [7:0] gap_1_data_out;

  // Probe on gap_1_data_out
  Clock clock_1 (.out(clock_1_out));
  GAP gap_1 (
    .RST(RST), .SEL(nSEL), .BUS_SEL(BUS_SEL__CHIP), .DATA_OUT(gap_1_data_out), .DATA_IN(DATA_IN),
    .D3_prime(BUS_SEL__other), .D2_prime(TSM_END__other), .D0_prime_D1_prime(DATA__D0_D1),
    .D3(BUS_SEL__other), .D2(TSM_END__other), .D0_D1(DATA__D0_D1), .CLK(clock_1_out));
  // Probe on DATA__D0_D1

  // Notes on the sheet:
  //   DATA OUT
endmodule

module MiniComputer (
);

  wire cpu_1_p1, cpu_1_p2, not_1_out, not_2_out, pc_1_gap1, pc_1_gap2, pc_1_pmg, Power_Button_out, undriven_2;
  wire [2:0] cpu_1_p4;
  wire [7:0] cpu_1_p5, gap_1_data_out, pc_1_application_program, pc_1_data_to_port_prime, undriven;

  LED Status (.in(cpu_1_p1));
  not not_1 (not_1_out, pc_1_gap1);
  Button Power_Button (.out(Power_Button_out));
  // CPU cpu_1: pin names not known; wires that end beside it: cpu_1_p1, cpu_1_p2, Power_Button_out, cpu_1_p4, cpu_1_p5
  GAP gap_1 (
    .RST(not_1_out), .SEL(pc_1_gap1), .DATA_OUT(gap_1_data_out), .DATA_IN(pc_1_data_to_port_prime),
    .CLK(cpu_1_p2));  // open: BUS_SEL, D3_prime, D2_prime, D0_prime_D1_prime, D3, D2, D0_D1
  PC pc_1 (
    .SEL(undriven_2), .DATA_TO_PORT(undriven), .INSTR(cpu_1_p4), .DATA_FROM_PORT_prime(cpu_1_p5),
    .DATA_TO_PORT_prime(pc_1_data_to_port_prime), .DATA_FROM_PORT(gap_1_data_out), .GAP1(pc_1_gap1),
    .GAP2(pc_1_gap2), .PMG(pc_1_pmg), .APPLICATION_PROGRAM(pc_1_application_program));
  not not_2 (not_2_out, pc_1_gap2);
  ROMChip romchip_1 ();  // open: Select, Address
  RAMChip ramchip_1 ();  // open: Address, Data_IN, Select, Store, Read, Clear, Data_OUT
  GAP gap_2 (
    .RST(not_2_out), .SEL(pc_1_gap2), .DATA_OUT(gap_1_data_out), .DATA_IN(pc_1_data_to_port_prime),
    .CLK(cpu_1_p2));  // open: BUS_SEL, D3_prime, D2_prime, D0_prime_D1_prime, D3, D2, D0_D1
endmodule

module CPU (
  input  Computer_ON,
  input  [7:0] Command_Byte,
  input  [9:0] Source,
  input  [31:0] Data,
  input  [31:0] ALU_Result,
  output Computer_Status,
  output Clock,
  output Instruction_processed,
  output [31:0] DATA_OUT,
  output [9:0] Select,
  output [31:0] R1_Register,
  output [31:0] R2_Register,
  output HSD_0x08,
  output SHD_0x09,
  output MOV_0x61,
  output JMP_0x42,
  output ADD_0x63,
  output SUB_0x64,
  output MUL_0x65,
  output DIV_0x66,
  output CMP_0x67
);

  wire and_1_out, and_2_out, and_3_out, and_4_out, buffer_1_out, Clock_out, comparator_1_eq, counter_1_carry,
       decoder_2_out1, decoder_2_out2, decoder_2_out3, INSTR_RST, not_1_out, or_1_out, or_2_out, or_3_out,
       t_ff_2_q, t_ff_3_q, t_ff_3_qn, t_ff_5_q, undriven;
  wire [1:0] counter_1_q;
  wire [2:0] bitadder_1_out;
  wire [6:0] controlled_buffer_2_out, controlled_buffer_4_out, controlled_buffer_5_out;
  wire [7:0] controlled_buffer_7_out, register_1_q, register_2_q;
  wire [9:0] controlled_buffer_9_out, register_3_q;
  wire [31:0] controlled_buffer_10_out;

  Pull_Resistor pull_resistor_1 (.node(MOV_0x61));
  Clock u_Clock (.out(Clock_out));
  assign Clock = Computer_Status ? Clock_out : 1'bz;  // Controlled_Buffer controlled_buffer_1
  Pull_Resistor pull_resistor_2 (.node(Clock));
  Pull_Resistor pull_resistor_3 (.node(JMP_0x42));
  Pull_Resistor pull_resistor_4 (.node(Computer_ON));
  Decoder #(.select(4), .disabled(0)) decoder_1 (
    .out1(MOV_0x61), .out2(JMP_0x42), .out3(ADD_0x63), .out4(SUB_0x64), .out5(MUL_0x65), .out6(DIV_0x66),
    .out7(CMP_0x67), .out8(HSD_0x08), .out9(SHD_0x09), .sel(controlled_buffer_2_out[3:0]),
    .en(Computer_Status));  // open: out0, out10, out11, out12, out13, out14, out15
  Pull_Resistor pull_resistor_5 (.node(ADD_0x63));
  Pull_Resistor pull_resistor_6 (.node(Computer_Status));
  T_Flip_Flop t_ff_1 (.clk(Computer_ON), .T(Computer_ON), .Q(Computer_Status), .en(1'b1));  // open: Qn, preset, reset
  Pull_Resistor pull_resistor_7 (.node(MUL_0x65));
  Pull_Resistor pull_resistor_8 (.node(SUB_0x64));
  assign controlled_buffer_2_out = decoder_2_out1 ? controlled_buffer_4_out : 7'bz;  // Controlled_Buffer controlled_buffer_2
  Pull_Resistor pull_resistor_9 (.node(CMP_0x67));
  Pull_Resistor pull_resistor_10 (.node(DIV_0x66));
  Decoder #(.select(2), .disabled(0)) decoder_2 (
    .out0(INSTR_RST), .out1(decoder_2_out1), .out2(decoder_2_out2), .out3(decoder_2_out3), .sel(counter_1_q),
    .en(Computer_Status));
  not not_1 (not_1_out, Computer_Status);
  T_Flip_Flop t_ff_2 (
    .Q(t_ff_2_q), .preset(controlled_buffer_2_out[6]), .reset(counter_1_carry), .en(Computer_Status));  // open: clk, T, Qn
  T_Flip_Flop t_ff_3 (
    .Q(t_ff_3_q), .Qn(t_ff_3_qn), .preset(controlled_buffer_2_out[5]), .reset(counter_1_carry),
    .en(Computer_Status));  // open: clk, T
  assign R1_Register = t_ff_3_q ? controlled_buffer_10_out : 32'bz;  // Controlled_Buffer controlled_buffer_3
  or or_1 (or_1_out, ADD_0x63, SUB_0x64, MUL_0x65, DIV_0x66, CMP_0x67);
  T_Flip_Flop t_ff_4 (.preset(or_1_out));  // open: clk, T, Q, Qn, reset, en
  assign controlled_buffer_4_out = t_ff_5_q ? controlled_buffer_7_out[6:0] : 7'bz;  // Controlled_Buffer controlled_buffer_4
  Counter #(.width(2), .max('h3)) counter_1 (
    .Q(counter_1_q), .carry(counter_1_carry), .clk(Clock), .clr(not_1_out));  // open: load, D, count
  and and_1 (and_1_out, decoder_2_out3, t_ff_2_q);
  and and_2 (and_2_out, decoder_2_out2, t_ff_3_q);
  Pull_Resistor pull_resistor_11 (.node(SHD_0x09));
  Pull_Resistor pull_resistor_12 (.node(HSD_0x08));
  BitAdder #(.width(7)) bitadder_1 (.in0(controlled_buffer_7_out[6:0]), .out(bitadder_1_out));
  Pull_Resistor pull_resistor_13 (.node(controlled_buffer_7_out[7]));
  T_Flip_Flop t_ff_5 (
    .Q(t_ff_5_q), .preset(or_2_out), .reset(counter_1_carry), .en(Computer_Status));  // open: clk, T, Qn
  and and_3 (and_3_out, ~bitadder_1_out[0], controlled_buffer_7_out[7]);  // AND_Gate
  Register #(.trigger("high")) register_1 (
    .D(controlled_buffer_7_out), .en(and_2_out), .Q(register_1_q), .clk(Clock));  // open: clr
  Pull_Resistor pull_resistor_14 (.node(register_1_q[6:0]));
  assign controlled_buffer_5_out = t_ff_3_q ? register_1_q[6:0] : 7'bz;  // Controlled_Buffer controlled_buffer_5
  buf buffer_1 (buffer_1_out, register_1_q[7]);
  assign R2_Register = t_ff_2_q ? controlled_buffer_10_out : 32'bz;  // Controlled_Buffer controlled_buffer_6
  assign controlled_buffer_7_out = Computer_Status ? Command_Byte : 8'bz;  // Controlled_Buffer controlled_buffer_7
  or or_2 (or_2_out, and_3_out, and_4_out);
  Pull_Resistor pull_resistor_15 (.node(controlled_buffer_7_out));
  Register #(.trigger("high")) register_2 (
    .D(controlled_buffer_7_out), .en(and_1_out), .Q(register_2_q), .clk(Clock));  // open: clr
  Pull_Resistor pull_resistor_16 (.node(register_2_q[6:0]));
  assign controlled_buffer_5_out = t_ff_2_q ? register_2_q[6:0] : 7'bz;  // Controlled_Buffer controlled_buffer_8
  buf buffer_2 (buffer_1_out, register_2_q[7]);
  Decoder #(.disabled(0)) decoder_3 (.out0(Select[0]), .out1(Select[1]), .sel(buffer_1_out), .en(or_3_out));
  or or_3 (or_3_out, t_ff_2_q, t_ff_3_q);
  and and_4 (and_4_out, bitadder_1_out[0], ~controlled_buffer_7_out[7]);  // AND_Gate
  assign DATA_OUT = {{25{1'b0}}, controlled_buffer_5_out};  // Bit_Extender bit_extender_1
  assign controlled_buffer_9_out = comparator_1_eq ? Source : 10'bz;  // Controlled_Buffer controlled_buffer_9
  assign controlled_buffer_10_out = comparator_1_eq ? Data : 32'bz;  // Controlled_Buffer controlled_buffer_10
  and and_5 (Instruction_processed, Clock, INSTR_RST, undriven);
  Pull_Resistor pull_resistor_17 (.node(Instruction_processed));
  Register #(.width(10)) register_3 (.D(Select), .en(Computer_Status), .Q(register_3_q));  // open: clk, clr
  Comparator #(.width(10), .mode("unsigned")) comparator_1 (
    .a(register_3_q), .b(Source), .eq(comparator_1_eq));  // open: gt, lt
  Pull_Resistor pull_resistor_18 (.node(comparator_1_eq));

  // Other names for the same wires on the sheet: CLK = Clock

  // Notes on the sheet:
  //   //Memory operations
  //   // ALU operations
  //   // Instruction code (1 Byte)
  //   //Flag - expect ALU result
  //   // Byte counter
  //   // Resolve address values
  //   // Ax
  //   // (OPTIONAL)
  //   // Ay
  //   //System operations
  //   // Parity check
  //   // --> Store the values in R1 and R2
  //   //  --> Memory addresses for X and Y
  //   // 4 Command Bits + 1 parity bit (bit7) or the optional X/Y arguments
  //   //Select chip: 0 = RAM Chip, 1 = ROM Chip
  //   // Expected responding chip
  //   // Command byte: Check the parity of bits 0-6 against bit 7 (1 if the number of bits = 1 is even, o otherwise)
  //   // --> The instruction was actually processed
endmodule

// GAP2
module GAP (
  input  BUS_SEL,
  input  [7:0] DATA_IN,
  input  CLK,
  input  RST,
  input  SEL,
  input  D3,
  input  D2,
  input  [1:0] D0_D1,
  output [7:0] DATA_OUT,
  output D3_prime,
  output D2_prime,
  output [1:0] D0_prime_D1_prime
);

  wire ACQ, and_1_out, and_2_out, and_3_out, and_5_out, buffer_5_out, comparator_1_eq,
       controlled_buffer_7_out, counter_1_carry, counter_2_carry, not_2_out, not_3_out, nSEL, or_1_out,
       or_2_out, or_3_out, or_4_out, pull_resistor_1_node, pull_resistor_3_node, RST_t, TSM2B;
  wire [1:0] controlled_buffer_1_out, controlled_buffer_4_out, register_2_q;
  wire [2:0] counter_1_q;
  wire [5:0] register_2_q_2;
  wire [7:0] adder_1_out, bit_extender_1_out, controlled_buffer_5_out, controlled_buffer_6_out, register_1_q,
       shifter_1_out, shifter_2_out;

  buf buffer_1 (RST_t, RST);
  not not_1 (nSEL, SEL);
  Counter #(.width(3), .max('h4)) counter_1 (
    .count(pull_resistor_3_node), .Q(counter_1_q), .carry(counter_1_carry), .clk(pull_resistor_3_node),
    .clr(or_1_out));  // open: load, D
  buf buffer_2 (D3_prime, BUS_SEL);
  and and_1 (and_1_out, counter_1_carry, ~and_3_out);  // AND_Gate
  Comparator #(.width(3)) comparator_1 (.a(counter_1_q), .b(3'b100), .eq(comparator_1_eq));  // open: gt, lt
  Shifter shifter_1 (.in(register_1_q), .\dist (3'b010), .out(shifter_1_out));
  Adder adder_1 (.a(shifter_1_out), .b(bit_extender_1_out), .out(adder_1_out));  // open: cin, cout
  assign bit_extender_1_out = {{6{1'b0}}, controlled_buffer_1_out};  // Bit_Extender bit_extender_1
  Pull_Resistor pull_resistor_1 (.node(pull_resistor_1_node));
  assign controlled_buffer_1_out = pull_resistor_1_node ? D0_D1 : 2'bz;  // Controlled_Buffer controlled_buffer_1
  and and_2 (and_2_out, BUS_SEL, TSM2B, ~counter_2_carry);  // AND_Gate
  buf buffer_3 (D2_prime, and_2_out);
  assign DATA_OUT = and_1_out ? register_1_q : 8'bz;  // Controlled_Buffer controlled_buffer_2
  Pull_Resistor pull_resistor_2 (.node(BUS_SEL));
  Register register_1 (
    .D(adder_1_out), .en(pull_resistor_3_node), .Q(register_1_q), .clk(pull_resistor_3_node), .clr(or_1_out));
  and and_3 (and_3_out, comparator_1_eq, ~pull_resistor_3_node);  // AND_Gate
  or or_1 (or_1_out, and_3_out, RST_t);
  Pull_Resistor pull_resistor_3 (.node(pull_resistor_3_node));
  and and_4 (pull_resistor_1_node, nSEL, ~ACQ, D3);  // AND_Gate
  assign pull_resistor_3_node = pull_resistor_1_node ? buffer_5_out : 1'bz;  // Controlled_Buffer controlled_buffer_3
  assign controlled_buffer_4_out = and_2_out ? register_2_q : 2'bz;  // Controlled_Buffer controlled_buffer_4
  assign D0_prime_D1_prime = controlled_buffer_4_out;  // Buffer buffer_4, 2 bits wide
  not not_2 (not_2_out, BUS_SEL);
  Counter #(.width(4), .max('h5), .ongoal("stay")) counter_2 (
    .count(TSM2B), .carry(counter_2_carry), .clk(TSM2B), .clr(or_4_out));  // open: load, D, Q
  buf buffer_5 (buffer_5_out, D2);
  assign controlled_buffer_5_out = not_2_out ? DATA_IN : 8'bz;  // Controlled_Buffer controlled_buffer_5
  Register #(.trigger("falling")) register_2 (
    .D(controlled_buffer_5_out), .en(or_2_out), .Q({register_2_q_2, register_2_q}),
    .clk(controlled_buffer_7_out), .clr(or_3_out));
  or or_2 (or_2_out, not_2_out, TSM2B);
  or or_3 (or_3_out, RST_t, counter_2_carry);
  or or_4 (or_4_out, ~BUS_SEL, RST_t);  // OR_Gate
  assign controlled_buffer_6_out = TSM2B ? {register_2_q_2, register_2_q} : 8'bz;  // Controlled_Buffer controlled_buffer_6
  Shifter #(.shift("lr")) shifter_2 (.in(controlled_buffer_6_out), .\dist (3'b010), .out(shifter_2_out));
  Pull_Resistor pull_resistor_4 (.node(D3));
  and and_5 (and_5_out, ~D3, BUS_SEL);  // AND_Gate
  not not_3 (not_3_out, BUS_SEL);
  assign controlled_buffer_7_out = nSEL ? CLK : 1'bz;  // Controlled_Buffer controlled_buffer_7
  assign controlled_buffer_5_out = BUS_SEL ? shifter_2_out : 8'bz;  // Controlled_Buffer controlled_buffer_8
  Pull_Resistor pull_resistor_5 (.node(TSM2B));
  Pull_Resistor pull_resistor_6 (.node(ACQ));
  D_Flip_Flop d_ff_1 (.Q(ACQ), .preset(and_5_out), .en(and_5_out), .reset(not_3_out));  // open: clk, D, Qn
  and and_6 (TSM2B, ACQ, CLK);

  // Notes on the sheet:
  //   //Receive counter
  //   buffer_2 drives only 1 and floats otherwise
  //   //Bus select
  //   buffer_3 drives only 1 and floats otherwise
  //   //Tsm end (2 bits)
  //   //Outputs to the bus
  //   //Output to the chip
  //   //Data
  //   //Tsm end
  //   //Bus select
  //   //Input from the chip
  //   //Data
  //   //Inputs from the bus
  //   //Bus acquired
  //   //1 = This chip transmits
endmodule

module ALU (
  input  ADD,
  input  SUB,
  input  JMP,
  input  DIV,
  input  CMP,
  input  MUL,
  input  [31:0] IN1,
  input  [31:0] IN2
);

  wire comparator_1_gt, comparator_1_lt;
  wire [7:0] controlled_buffer_1_out, controlled_buffer_3_out, controlled_buffer_4_out, pull_resistor_4_node,
       subtractor_1_out;

  Shifter #(.width(23)) shifter_1 ();  // open: in, dist, out
  assign controlled_buffer_1_out = comparator_1_lt ? IN1[31:24] : 8'bz;  // Controlled_Buffer controlled_buffer_1
  Pull_Resistor pull_resistor_1 (.node(controlled_buffer_1_out));
  Shifter #(.width(32)) shifter_2 ();  // open: in, dist, out
  assign controlled_buffer_1_out = comparator_1_gt ? IN2[31:24] : 8'bz;  // Controlled_Buffer controlled_buffer_2
  Comparator comparator_1 (
    .a(IN1[31:24]), .b(IN2[31:24]), .gt(comparator_1_gt), .eq(comparator_1_gt), .lt(comparator_1_lt));
  Subtractor subtractor_1 (.a(IN1[31:24]), .b(IN2[31:24]), .out(subtractor_1_out));  // open: bin, bout
  Pull_Resistor pull_resistor_2 (.node(comparator_1_gt));
  assign controlled_buffer_3_out = comparator_1_gt ? subtractor_1_out : 8'bz;  // Controlled_Buffer controlled_buffer_3
  Pull_Resistor pull_resistor_3 (.node(controlled_buffer_3_out));
  Pull_Resistor pull_resistor_4 (.node(pull_resistor_4_node));
  Subtractor subtractor_2 (.a(IN2[31:24]), .b(IN1[31:24]), .out(pull_resistor_4_node));  // open: bin, bout
  Pull_Resistor pull_resistor_5 (.node(comparator_1_lt));
  assign controlled_buffer_4_out = comparator_1_lt ? pull_resistor_4_node : 8'bz;  // Controlled_Buffer controlled_buffer_4
  Pull_Resistor pull_resistor_6 (.node(controlled_buffer_4_out));

  // Other names for the same wires on the sheet: S1 = IN1[0]; M1[22:0] = IN1[23:1]; S2 = IN2[0]; M2[22:0] = IN2[23:1]

  // Notes on the sheet:
  //   E1>=E2
  //   E1<E2
endmodule

// RAM
module RAMChip (
  input  [11:0] Address,
  input  [31:0] Data_IN,
  input  [9:0] Select,
  input  Store,
  input  Read,
  input  Clear,
  output [31:0] Data_OUT
);

  Pull_Resistor pull_resistor_1 (.node(Select));
  RAM #(.addrWidth(12), .dataWidth(32), .bus("separate")) ram_1 (
    .addr(Address), .din(Data_IN), .data(Data_OUT), .str(Store), .sel(Select[0]), .ld(Read), .clr(Clear));  // open: clk

  // Notes on the sheet:
  //   // 4.096 bytes of RAM
endmodule

// ROM
module ROMChip (
  input  Select,
  input  Address
);

  ROM rom_1 ();  // open: addr, data, sel
endmodule

module PC (
  input  [7:0] DATA_TO_PORT,
  input  [2:0] INSTR,
  input  SEL,
  input  [7:0] DATA_FROM_PORT,
  output [7:0] DATA_FROM_PORT_prime,
  output PMG,
  output [7:0] APPLICATION_PROGRAM,
  output [7:0] DATA_TO_PORT_prime,
  output GAP1,
  output GAP2
);

  wire comparator_1_eq, t_ff_1_qn;

  assign DATA_TO_PORT_prime = SEL ? DATA_TO_PORT : 8'bz;  // Controlled_Buffer controlled_buffer_1
  Pull_Resistor pull_resistor_1 (.node(INSTR));
  Pull_Resistor pull_resistor_2 (.node(SEL));
  assign DATA_FROM_PORT_prime = t_ff_1_qn ? DATA_FROM_PORT : 8'bz;  // Controlled_Buffer controlled_buffer_2
  Comparator comparator_1 (.a(8'h6f), .b(DATA_FROM_PORT), .eq(comparator_1_eq));  // open: gt, lt
  T_Flip_Flop t_ff_1 (
    .clk(comparator_1_eq), .T(comparator_1_eq), .Q(PMG), .Qn(t_ff_1_qn), .en(SEL));  // open: preset, reset
  assign APPLICATION_PROGRAM = PMG ? DATA_FROM_PORT : 8'bz;  // Controlled_Buffer controlled_buffer_3

  assign GAP1 = INSTR[0];
  assign GAP2 = INSTR[1];

  // Notes on the sheet:
  //   //Port Controller
  //   //Instruction from the uC
  //   //Instruction from the uC
  //   //is being programmed
  //   //Control data transmission
  //   //Determine if a new application
  //   //GAP selection (1 = selected, 0 = de-selected)
  //   // --> Data from the selected ports, forwarded to the rest of the uC
  //   //Marks if a new application is being programmed (1)
endmodule
